// Logisim project 6597336.circ as structural Verilog: 1 circuit, main circuit main
module main (
  input  c,
  input  [1:0] ab,
  input  a,
  input  [1:0] bc,
  output a_prime_b_prime_c,
  output a_prime_bc,
  output abc,
  output F1,
  output a_prime_b_prime,
  output ab_prime,
  output ab_2,
  output b_prime_ca,
  output bc_prime_a,
  output bca,
  output F2,
  output b_prime_c_prime,
  output b_prime_c,
  output bc_prime
);

  wire a_prime_b_out, ab_prime_c_out, b_prime_c_prime_a_out, bc_out, decoder_1_out2, decoder_2_out1,
       decoder_3_out0, decoder_4_out3;

  Decoder #(.select(2)) decoder_1 (
    .out0(a_prime_b_prime_c), .out1(a_prime_bc), .out2(decoder_1_out2), .out3(abc), .sel(ab), .en(c));
  Decoder #(.select(2), .enable("false")) decoder_2 (
    .out0(a_prime_b_prime), .out1(decoder_2_out1), .out2(ab_prime), .out3(ab_2), .sel(ab));
  Decoder #(.select(2)) decoder_3 (
    .out0(decoder_3_out0), .out1(b_prime_ca), .out2(bc_prime_a), .out3(bca), .sel(bc), .en(a));
  Decoder #(.select(2), .enable("false")) decoder_4 (
    .out0(b_prime_c_prime), .out1(b_prime_c), .out2(bc_prime), .out3(decoder_4_out3), .sel(bc));
  buf b_prime_c_prime_a (b_prime_c_prime_a_out, decoder_3_out0);
  buf u_bc (bc_out, decoder_4_out3);
  buf ab_prime_c (ab_prime_c_out, decoder_1_out2);
  buf a_prime_b (a_prime_b_out, decoder_2_out1);
  or or_1 (F1, ab_prime_c_out, a_prime_b_out);
  or or_2 (F2, b_prime_c_prime_a_out, bc_out);

  // Notes on the sheet:
  //   HW4 - Question 1
  //   Harun Yahya Demirpençe
  //   150210022
  //   2:4 Decoder
  //   2:4 Decoder
  //   2:4 Decoder
  //   2:4 Decoder
  //   EN
  //   EN
endmodule
