// Logisim project 6597337.circ as structural Verilog: 1 circuit, main circuit main
module main (
  input  [3:0] A,
  input  [3:0] B,
  input  [3:0] C,
  input  Y,
  input  X,
  output [3:0] Z
);

  wire [3:0] multiplexer_1_out, multiplexer_2_out, not_1_out;

  Multiplexer #(.width(4), .enable("false")) multiplexer_1 (.in0(C), .in1(A), .out(multiplexer_1_out), .sel(Y));
  assign not_1_out = ~B;  // NOT_Gate not_1, 4 bits wide
  Adder #(.width(4)) adder_1 (.a(multiplexer_2_out), .b(multiplexer_1_out), .out(Z), .cin(X));  // open: cout
  Multiplexer #(.width(4), .enable("false")) multiplexer_2 (.in0(C), .in1(not_1_out), .out(multiplexer_2_out), .sel(X));

  // Notes on the sheet:
  //   HW4 - Question 2
  //   Harun Yahya Demirpençe
  //   150210022
  //   C
  //   A
  //   4-bit 2:1 MUX
  //   4-bit Parallel Adder
  //   C
  //   B'
endmodule
